# Fritzing sketch streetlights (saved by Fritzing 0.9.6b)
breadboards: 1

parts:
  Part1 = Arduino Uno (Rev3) - ICSP
  R1 = Resistor [tolerance=±5% resistance=220 package=THT]
  LED1 = LED - 5mm [color="Yellow (595nm)" package="5 mm [THT]"]
  J1 = Piezo Speaker
  R2 = Photocell (LDR) [package=THT]
  R3 = Resistor [tolerance=±5% resistance=220 package=THT]
  R4 = Resistor [tolerance=±5% resistance=220 package=THT]

nets:
  N1: Part1.A0, R2.pin_1, R4.Pin_0
  N2: Part1.A1, J1.pin2, R3.Pin_1
  N3: Part1.5V, R1.Pin_0, R2.pin_0
  N4: Part1.GND, LED1.anode, J1.pin1, R3.Pin_0, R4.Pin_1
  N5: R1.Pin_1, LED1.cathode
